# Fritzing sketch solenoid_valve (saved by Fritzing 0.8.7b)

parts:
  VALVE3 = Plastic Solenoid Valve
  D3 = Diode [package=diode-1n4001]
  R16 = Resistor [tolerance=±5% resistance=10k package="1206 [SMD]"]
  JACK3 = 2.1mm Barrel Jack with Terminal Block
  U7 = ESP8266 NodeMCU LoLin module
  FET3 = STP16NF06 N-Channel Power MOSFET

nets:
  N1: VALVE3.no_name_yet#1, D3.C, FET3.source
  N2: VALVE3.no_name_yet#2, D3.A, JACK3.POS
  N3: R16.Pin_0, U7.D2
  N4: R16.Pin_1, FET3.gate
  N5: JACK3.NEG, U7.GND, FET3.drain

custom parts:
  ESP8266 NodeMCU LoLin module: ESP8266 based NodeMCU
  STP16NF06 N-Channel Power MOSFET: STP16NF06 N-channel Power MOSFET
